# Fritzing sketch Skematik (saved by Fritzing 0.9.3b)

parts:
  M1 = ESP32-S3-DevKitC-1-N8R8-v1 [part_number=ESP32-S3-DevKitC-1-N8R8-v1]
  JACK1 = 2.1mm Barrel Jack with Terminal Block
  R1 = Resistor [tolerance=±5% resistance=220 package="0805 [SMD]"]
  R2 = Resistor [tolerance=±5% resistance=220 package=THT]
  U1 = 2-Channel 5v Relay Shield [package=relay-2ch5v10a]
  S1 = KY-026
  DHT1 = DHT22 Humidity and Temperature Sensor
  Part1 = MQ-7 breakout
  A1 = ZS-042 Real Time Clock Module
  J1 = Buzzer

nets:
  N1: M1.pin_1, M1.pin_2, S1.pin3, DHT1.VDD
  N2: M1.pin_8, A1.SDA
  N3: M1.pin_9, A1.SCL
  N4: M1.pin_14, J1.pin1
  VCC: M1.pin_21, JACK1.POS, U1.VCC, Part1.VCC, A1.VCC
  GND: M1.pin_22, M1.pin_23, M1.pin_44, JACK1.NEG, R1.Pin_1, S1.pin2, DHT1.GND, A1.GND, J1.pin2
  N5: M1.pin_27, R2.Pin_0
  N6: M1.pin_29, S1.pin4
  N7: M1.pin_31, U1.IN1
  N8: M1.pin_32, U1.IN2
  N9: M1.pin_33, DHT1.DATA
  N10: R2.Pin_1, Part1.AO
  N11: U1.K1-On, U1.K2-In, U1.K2-Off, U1.JD-GND

custom parts:
  ESP32-S3-DevKitC-1-N8R8-v1: ESP32-S3-DevKitC-1-N8R8-v1 This module is 44pins long (2x22) and 11 pins width.
  2-Channel 5v Relay Shield: 2 Channel 5v Relay Shield w. 2x SPD-06VDC-SD-C
  KY-026: ky-026 flame sensor module
  MQ-7 breakout: SKU: 101282
  Buzzer: Fixed frequency buzzer
